# Fritzing sketch FYP Sketch 1 (saved by Fritzing 1.0.4)
breadboards: 1

parts:
  V2 = DC Power [voltage=12V internal_resistance=0.1Ω]
  D1 = SOLAR-IXYS [package=solarbit-12x1]
  D2 = SOLAR-IXYS [package=solarbit-12x1]  # not connected
  D3 = SOLAR-IXYS [package=solarbit-12x1]  # not connected
  D4 = SOLAR-IXYS [package=solarbit-12x1]
  D5 = SOLAR-IXYS [package=solarbit-12x1]  # not connected
  D6 = SOLAR-IXYS [package=solarbit-12x1]  # not connected
  D7 = SOLAR-IXYS [package=solarbit-12x1]  # not connected
  D8 = SOLAR-IXYS [package=solarbit-12x1]  # not connected
  D9 = SOLAR-IXYS [package=solarbit-12x1]
  D10 = SOLAR-IXYS [package=solarbit-12x1]
  D11 = SOLAR-IXYS [package=solarbit-12x1]
  D12 = SOLAR-IXYS [package=solarbit-12x1]  # not connected
  D13 = SOLAR-IXYS [package=solarbit-12x1]  # not connected
  D14 = SOLAR-IXYS [package=solarbit-12x1]  # not connected
  D15 = SOLAR-IXYS [package=solarbit-12x1]
  D16 = SOLAR-IXYS [package=solarbit-12x1]
  D17 = SOLAR-IXYS [package=solarbit-12x1]  # not connected
  D18 = SOLAR-IXYS [package=solarbit-12x1]  # not connected
  D19 = SOLAR-IXYS [package=solarbit-12x1]  # not connected
  D20 = SOLAR-IXYS [package=solarbit-12x1]
  Voltage_regulator = LMZ14203 [package=to-pmod-7]
  Charge_Controller_12V = SO08w [chip_label=SO08w package=SO(w)]
  Arduino_GIGA_R1 = Arduino Mega 2560 (Rev3)
  H-Bridge_Motor_Driver = Dual VNH2SP30 Motor Driver [part_number=MD03A]
  Y_AXIS = Basic Servo
  Y_AXIS_2 = Basic Servo  # not connected
  X_AXIS = Basic Servo
  Linear_Actuator = DC Motor [voltage_(max)=12V voltage_(min)=3V]
  DC_Propeller = DC Motor [voltage_(max)=6V voltage_(min)=3V]
  R1 = Photocell (LDR) [power=0.25W dark_resistance_@0.01lx=300kΩ light_resistance_@100lx=400Ω luminance=10lx package=THT]
  R2 = Photocell (LDR) [power=0.25W dark_resistance_@0.01lx=300kΩ light_resistance_@100lx=400Ω luminance=10lx package=THT]
  R3 = Photocell (LDR) [power=0.25W dark_resistance_@0.01lx=300kΩ light_resistance_@100lx=400Ω luminance=10lx package=THT]
  R4 = Photocell (LDR) [power=0.25W dark_resistance_@0.01lx=300kΩ light_resistance_@100lx=400Ω luminance=10lx package=THT]
  Flyback_Diode = Diode [package=smb-diode]
  R5 = Resistor [tolerance=±5% resistance=10k package="0402 [SMD]"]
  R6 = Resistor [tolerance=±5% resistance=10k package="0402 [SMD]"]
  R7 = Resistor [tolerance=±5% resistance=10k package="0402 [SMD]"]
  R8 = Resistor [tolerance=±5% resistance=10k package="0402 [SMD]"]
  F1 = FUSE [package=fuse_5mm]

nets:
  N1: V2.V-, Charge_Controller_12V.4, F1.1
  N2: V2.V+, Charge_Controller_12V.3, F1.2
  N3: D1.A, D4.A, D11.A, D16.A, Charge_Controller_12V.1
  N4: D9.C, D10.C, D15.C, D20.C, Charge_Controller_12V.2
  N5: Voltage_regulator.VIN, Charge_Controller_12V.5
  GND: Voltage_regulator.GND, Y_AXIS.pulse, X_AXIS.gnd
  VCC: Voltage_regulator.VOUT, Y_AXIS.vcc, X_AXIS.vcc
  N6: Charge_Controller_12V.6, H-Bridge_Motor_Driver.Pin_8
  N7: Charge_Controller_12V.7, H-Bridge_Motor_Driver.Pin_7
  N8: Charge_Controller_12V.8, Arduino_GIGA_R1.5V, R1.pin_0, R2.pin_0, R4.pin_0
  N9: Arduino_GIGA_R1.A0, R4.pin_1, R5.Pin_0
  N10: Arduino_GIGA_R1.A1, R2.pin_1, R8.Pin_0
  N11: Arduino_GIGA_R1.A2, R3.pin_1, R6.Pin_0
  N12: Arduino_GIGA_R1.A3, R1.pin_1, R7.Pin_0
  N13: Arduino_GIGA_R1.GND, R5.Pin_1, R6.Pin_1, R7.Pin_1, R8.Pin_1
  N14: H-Bridge_Motor_Driver.Pin_16, DC_Propeller.pin_2
  N15: H-Bridge_Motor_Driver.Pin_17, DC_Propeller.pin_1
  N16: H-Bridge_Motor_Driver.Pin_20, Linear_Actuator.pin_2, Flyback_Diode.A
  N17: H-Bridge_Motor_Driver.Pin_21, Linear_Actuator.pin_1, Flyback_Diode.C
